// Logisim project t_triger.circ as structural Verilog: 1 circuit, main circuit main
module main (
  input  in_1,
  input  in_2,
  output out_3,
  output [2:0] out_4,
  output out_5,
  output out_6
);

  wire and_1_out, nand_1_out, nand_2_out, nand_3_out, nand_4_out, nand_5_out, nand_6_out, nand_7_out,
       nand_8_out, nand_9_out, nand_10_out, nand_11_out, nand_12_out, nand_13_out, nand_14_out, nand_15_out,
       nand_16_out, nand_17_out, nand_18_out, nand_19_out, nand_21_out, nand_23_out;

  nand nand_1 (nand_1_out, out_3, in_1, in_2);
  nand nand_2 (nand_2_out, in_2, in_1, nand_19_out);
  nand nand_3 (nand_3_out, out_4[1], out_3, in_2);
  nand nand_4 (nand_4_out, in_2, out_3, nand_21_out);
  nand nand_5 (nand_5_out, out_4[2], and_1_out, in_2);
  nand nand_6 (nand_6_out, in_2, and_1_out, nand_23_out);
  nand nand_7 (nand_7_out, nand_1_out, nand_8_out);
  nand nand_8 (nand_8_out, nand_7_out, nand_2_out);
  nand nand_9 (nand_9_out, nand_3_out, nand_10_out);
  nand nand_10 (nand_10_out, nand_9_out, nand_4_out);
  nand nand_11 (nand_11_out, nand_5_out, nand_12_out);
  nand nand_12 (nand_12_out, nand_11_out, nand_6_out);
  nand nand_13 (nand_13_out, nand_1_out, nand_7_out);
  nand nand_14 (nand_14_out, nand_8_out, nand_2_out);
  nand nand_15 (nand_15_out, nand_3_out, nand_9_out);
  nand nand_16 (nand_16_out, nand_10_out, nand_4_out);
  nand nand_17 (nand_17_out, nand_5_out, nand_11_out);
  nand nand_18 (nand_18_out, nand_12_out, nand_6_out);
  nand nand_19 (nand_19_out, nand_13_out, out_3);
  nand nand_20 (out_3, nand_19_out, nand_14_out);
  nand nand_21 (nand_21_out, nand_15_out, out_4[1]);
  nand nand_22 (out_4[1], nand_21_out, nand_16_out);
  nand nand_23 (nand_23_out, nand_17_out, out_4[2]);
  nand nand_24 (out_4[2], nand_23_out, nand_18_out);
  and and_1 (and_1_out, out_3, out_4[1]);

  assign out_4[0] = out_3;
  assign out_5 = out_4[1];
  assign out_6 = out_4[2];
endmodule
